// Logisim project CPU.circ as structural Verilog
module RAM16 (
  input  addr1,
  input  addr2,
  input  addr3,
  input  addr4,
  input  EnableWrite,
  input  CLK,
  input  b1,
  input  b2,
  input  b3,
  input  b4,
  input  b5,
  input  b6,
  input  b7,
  input  b8,
  output o1,
  output o2,
  output o3,
  output o4,
  output o5,
  output o6,
  output o7,
  output o8
);

  wire and_1_out, and_2_out, and_3_out, and_4_out, and_5_out, and_6_out, and_7_out, and_8_out, and_9_out,
       and_10_out, and_11_out, and_12_out, and_13_out, and_14_out, and_15_out, and_16_out, byte_storage_1_o1,
       byte_storage_1_o2, byte_storage_1_o3, byte_storage_1_o4, byte_storage_1_o5, byte_storage_1_o6,
       byte_storage_1_o7, byte_storage_1_o8, byte_storage_2_o1, byte_storage_2_o2, byte_storage_2_o3,
       byte_storage_2_o4, byte_storage_2_o5, byte_storage_2_o6, byte_storage_2_o7, byte_storage_2_o8,
       byte_storage_3_o1, byte_storage_3_o2, byte_storage_3_o3, byte_storage_3_o4, byte_storage_3_o5,
       byte_storage_3_o6, byte_storage_3_o7, byte_storage_3_o8, byte_storage_4_o1, byte_storage_4_o2,
       byte_storage_4_o3, byte_storage_4_o4, byte_storage_4_o5, byte_storage_4_o6, byte_storage_4_o7,
       byte_storage_4_o8, byte_storage_5_o1, byte_storage_5_o2, byte_storage_5_o3, byte_storage_5_o4,
       byte_storage_5_o5, byte_storage_5_o6, byte_storage_5_o7, byte_storage_5_o8, byte_storage_6_o1,
       byte_storage_6_o2, byte_storage_6_o3, byte_storage_6_o4, byte_storage_6_o5, byte_storage_6_o6,
       byte_storage_6_o7, byte_storage_6_o8, byte_storage_7_o1, byte_storage_7_o2, byte_storage_7_o3,
       byte_storage_7_o4, byte_storage_7_o5, byte_storage_7_o6, byte_storage_7_o7, byte_storage_7_o8,
       byte_storage_8_o1, byte_storage_8_o2, byte_storage_8_o3, byte_storage_8_o4, byte_storage_8_o5,
       byte_storage_8_o6, byte_storage_8_o7, byte_storage_8_o8, byte_storage_9_o1, byte_storage_9_o2,
       byte_storage_9_o3, byte_storage_9_o4, byte_storage_9_o5, byte_storage_9_o6, byte_storage_9_o7,
       byte_storage_9_o8, byte_storage_10_o1, byte_storage_10_o2, byte_storage_10_o3, byte_storage_10_o4,
       byte_storage_10_o5, byte_storage_10_o6, byte_storage_10_o7, byte_storage_10_o8, byte_storage_11_o1,
       byte_storage_11_o2, byte_storage_11_o3, byte_storage_11_o4, byte_storage_11_o5, byte_storage_11_o6,
       byte_storage_11_o7, byte_storage_11_o8, byte_storage_12_o1, byte_storage_12_o2, byte_storage_12_o3,
       byte_storage_12_o4, byte_storage_12_o5, byte_storage_12_o6, byte_storage_12_o7, byte_storage_12_o8,
       byte_storage_13_o1, byte_storage_13_o2, byte_storage_13_o3, byte_storage_13_o4, byte_storage_13_o5,
       byte_storage_13_o6, byte_storage_13_o7, byte_storage_13_o8, byte_storage_14_o1, byte_storage_14_o2,
       byte_storage_14_o3, byte_storage_14_o4, byte_storage_14_o5, byte_storage_14_o6, byte_storage_14_o7,
       byte_storage_14_o8, byte_storage_15_o1, byte_storage_15_o2, byte_storage_15_o3, byte_storage_15_o4,
       byte_storage_15_o5, byte_storage_15_o6, byte_storage_15_o7, byte_storage_15_o8, byte_storage_16_o1,
       byte_storage_16_o2, byte_storage_16_o3, byte_storage_16_o4, byte_storage_16_o5, byte_storage_16_o6,
       byte_storage_16_o7, byte_storage_16_o8, decoder_1_out0, decoder_1_out1, decoder_1_out2,
       decoder_1_out3, decoder_1_out4, decoder_1_out5, decoder_1_out6, decoder_1_out7, decoder_1_out8,
       decoder_1_out9, decoder_1_out10, decoder_1_out11, decoder_1_out12, decoder_1_out13, decoder_1_out14,
       decoder_1_out15, not_1_out, read_passing_2_o1, read_passing_2_o2, read_passing_2_o3,
       read_passing_2_o4, read_passing_2_o5, read_passing_2_o6, read_passing_2_o7, read_passing_2_o8,
       read_passing_3_o1, read_passing_3_o2, read_passing_3_o3, read_passing_3_o4, read_passing_3_o5,
       read_passing_3_o6, read_passing_3_o7, read_passing_3_o8, read_passing_4_o1, read_passing_4_o2,
       read_passing_4_o3, read_passing_4_o4, read_passing_4_o5, read_passing_4_o6, read_passing_4_o7,
       read_passing_4_o8, read_passing_5_o1, read_passing_5_o2, read_passing_5_o3, read_passing_5_o4,
       read_passing_5_o5, read_passing_5_o6, read_passing_5_o7, read_passing_5_o8, read_passing_6_o1,
       read_passing_6_o2, read_passing_6_o3, read_passing_6_o4, read_passing_6_o5, read_passing_6_o6,
       read_passing_6_o7, read_passing_6_o8, read_passing_7_o1, read_passing_7_o2, read_passing_7_o3,
       read_passing_7_o4, read_passing_7_o5, read_passing_7_o6, read_passing_7_o7, read_passing_7_o8,
       read_passing_8_o1, read_passing_8_o2, read_passing_8_o3, read_passing_8_o4, read_passing_8_o5,
       read_passing_8_o6, read_passing_8_o7, read_passing_8_o8, read_passing_9_o1, read_passing_9_o2,
       read_passing_9_o3, read_passing_9_o4, read_passing_9_o5, read_passing_9_o6, read_passing_9_o7,
       read_passing_9_o8, read_passing_10_o1, read_passing_10_o2, read_passing_10_o3, read_passing_10_o4,
       read_passing_10_o5, read_passing_10_o6, read_passing_10_o7, read_passing_10_o8, read_passing_11_o1,
       read_passing_11_o2, read_passing_11_o3, read_passing_11_o4, read_passing_11_o5, read_passing_11_o6,
       read_passing_11_o7, read_passing_11_o8, read_passing_12_o1, read_passing_12_o2, read_passing_12_o3,
       read_passing_12_o4, read_passing_12_o5, read_passing_12_o6, read_passing_12_o7, read_passing_12_o8,
       read_passing_13_o1, read_passing_13_o2, read_passing_13_o3, read_passing_13_o4, read_passing_13_o5,
       read_passing_13_o6, read_passing_13_o7, read_passing_13_o8, read_passing_14_o1, read_passing_14_o2,
       read_passing_14_o3, read_passing_14_o4, read_passing_14_o5, read_passing_14_o6, read_passing_14_o7,
       read_passing_14_o8, read_passing_15_o1, read_passing_15_o2, read_passing_15_o3, read_passing_15_o4,
       read_passing_15_o5, read_passing_15_o6, read_passing_15_o7, read_passing_15_o8, read_passing_16_o1,
       read_passing_16_o2, read_passing_16_o3, read_passing_16_o4, read_passing_16_o5, read_passing_16_o6,
       read_passing_16_o7, read_passing_16_o8;

  not not_1 (not_1_out, EnableWrite);
  byte_storage byte_storage_1 (
    .o2(byte_storage_1_o2), .o3(byte_storage_1_o3), .o1(byte_storage_1_o1), .b8(b8), .b7(b7), .b6(b6),
    .b5(b5), .b4(b4), .b3(b3), .b2(b2), .b1(b1), .Enable(and_1_out), .Clock(CLK), .o4(byte_storage_1_o4),
    .o5(byte_storage_1_o5), .o6(byte_storage_1_o6), .o7(byte_storage_1_o7), .o8(byte_storage_1_o8));
  and and_1 (and_1_out, not_1_out, decoder_1_out0);
  byte_storage byte_storage_2 (
    .o2(byte_storage_2_o2), .o3(byte_storage_2_o3), .o1(byte_storage_2_o1), .b8(b8), .b7(b7), .b6(b6),
    .b5(b5), .b4(b4), .b3(b3), .b2(b2), .b1(b1), .Enable(and_2_out), .Clock(CLK), .o4(byte_storage_2_o4),
    .o5(byte_storage_2_o5), .o6(byte_storage_2_o6), .o7(byte_storage_2_o7), .o8(byte_storage_2_o8));
  and and_2 (and_2_out, not_1_out, decoder_1_out1);
  byte_storage byte_storage_3 (
    .o2(byte_storage_3_o2), .o3(byte_storage_3_o3), .o1(byte_storage_3_o1), .b8(b8), .b7(b7), .b6(b6),
    .b5(b5), .b4(b4), .b3(b3), .b2(b2), .b1(b1), .Enable(and_3_out), .Clock(CLK), .o4(byte_storage_3_o4),
    .o5(byte_storage_3_o5), .o6(byte_storage_3_o6), .o7(byte_storage_3_o7), .o8(byte_storage_3_o8));
  and and_3 (and_3_out, not_1_out, decoder_1_out2);
  byte_storage byte_storage_4 (
    .o2(byte_storage_4_o2), .o3(byte_storage_4_o3), .o1(byte_storage_4_o1), .b8(b8), .b7(b7), .b6(b6),
    .b5(b5), .b4(b4), .b3(b3), .b2(b2), .b1(b1), .Enable(and_4_out), .Clock(CLK), .o4(byte_storage_4_o4),
    .o5(byte_storage_4_o5), .o6(byte_storage_4_o6), .o7(byte_storage_4_o7), .o8(byte_storage_4_o8));
  and and_4 (and_4_out, not_1_out, decoder_1_out3);
  byte_storage byte_storage_5 (
    .o2(byte_storage_5_o2), .o3(byte_storage_5_o3), .o1(byte_storage_5_o1), .b8(b8), .b7(b7), .b6(b6),
    .b5(b5), .b4(b4), .b3(b3), .b2(b2), .b1(b1), .Enable(and_5_out), .Clock(CLK), .o4(byte_storage_5_o4),
    .o5(byte_storage_5_o5), .o6(byte_storage_5_o6), .o7(byte_storage_5_o7), .o8(byte_storage_5_o8));
  and and_5 (and_5_out, not_1_out, decoder_1_out4);
  byte_storage byte_storage_6 (
    .o2(byte_storage_6_o2), .o3(byte_storage_6_o3), .o1(byte_storage_6_o1), .b8(b8), .b7(b7), .b6(b6),
    .b5(b5), .b4(b4), .b3(b3), .b2(b2), .b1(b1), .Enable(and_6_out), .Clock(CLK), .o4(byte_storage_6_o4),
    .o5(byte_storage_6_o5), .o6(byte_storage_6_o6), .o7(byte_storage_6_o7), .o8(byte_storage_6_o8));
  and and_6 (and_6_out, not_1_out, decoder_1_out5);
  byte_storage byte_storage_7 (
    .o2(byte_storage_7_o2), .o3(byte_storage_7_o3), .o1(byte_storage_7_o1), .b8(b8), .b7(b7), .b6(b6),
    .b5(b5), .b4(b4), .b3(b3), .b2(b2), .b1(b1), .Enable(and_7_out), .Clock(CLK), .o4(byte_storage_7_o4),
    .o5(byte_storage_7_o5), .o6(byte_storage_7_o6), .o7(byte_storage_7_o7), .o8(byte_storage_7_o8));
  and and_7 (and_7_out, not_1_out, decoder_1_out6);
  byte_storage byte_storage_8 (
    .o2(byte_storage_8_o2), .o3(byte_storage_8_o3), .o1(byte_storage_8_o1), .b8(b8), .b7(b7), .b6(b6),
    .b5(b5), .b4(b4), .b3(b3), .b2(b2), .b1(b1), .Enable(and_8_out), .Clock(CLK), .o4(byte_storage_8_o4),
    .o5(byte_storage_8_o5), .o6(byte_storage_8_o6), .o7(byte_storage_8_o7), .o8(byte_storage_8_o8));
  and and_8 (and_8_out, not_1_out, decoder_1_out7);
  byte_storage byte_storage_9 (
    .o2(byte_storage_9_o2), .o3(byte_storage_9_o3), .o1(byte_storage_9_o1), .b8(b8), .b7(b7), .b6(b6),
    .b5(b5), .b4(b4), .b3(b3), .b2(b2), .b1(b1), .Enable(and_9_out), .Clock(CLK), .o4(byte_storage_9_o4),
    .o5(byte_storage_9_o5), .o6(byte_storage_9_o6), .o7(byte_storage_9_o7), .o8(byte_storage_9_o8));
  and and_9 (and_9_out, not_1_out, decoder_1_out8);
  byte_storage byte_storage_10 (
    .o2(byte_storage_10_o2), .o3(byte_storage_10_o3), .o1(byte_storage_10_o1), .b8(b8), .b7(b7), .b6(b6),
    .b5(b5), .b4(b4), .b3(b3), .b2(b2), .b1(b1), .Enable(and_10_out), .Clock(CLK), .o4(byte_storage_10_o4),
    .o5(byte_storage_10_o5), .o6(byte_storage_10_o6), .o7(byte_storage_10_o7), .o8(byte_storage_10_o8));
  and and_10 (and_10_out, not_1_out, decoder_1_out9);
  byte_storage byte_storage_11 (
    .o2(byte_storage_11_o2), .o3(byte_storage_11_o3), .o1(byte_storage_11_o1), .b8(b8), .b7(b7), .b6(b6),
    .b5(b5), .b4(b4), .b3(b3), .b2(b2), .b1(b1), .Enable(and_11_out), .Clock(CLK), .o4(byte_storage_11_o4),
    .o5(byte_storage_11_o5), .o6(byte_storage_11_o6), .o7(byte_storage_11_o7), .o8(byte_storage_11_o8));
  and and_11 (and_11_out, not_1_out, decoder_1_out10);
  byte_storage byte_storage_12 (
    .o2(byte_storage_12_o2), .o3(byte_storage_12_o3), .o1(byte_storage_12_o1), .b8(b8), .b7(b7), .b6(b6),
    .b5(b5), .b4(b4), .b3(b3), .b2(b2), .b1(b1), .Enable(and_12_out), .Clock(CLK), .o4(byte_storage_12_o4),
    .o5(byte_storage_12_o5), .o6(byte_storage_12_o6), .o7(byte_storage_12_o7), .o8(byte_storage_12_o8));
  and and_12 (and_12_out, not_1_out, decoder_1_out11);
  byte_storage byte_storage_13 (
    .o2(byte_storage_13_o2), .o3(byte_storage_13_o3), .o1(byte_storage_13_o1), .b8(b8), .b7(b7), .b6(b6),
    .b5(b5), .b4(b4), .b3(b3), .b2(b2), .b1(b1), .Enable(and_13_out), .Clock(CLK), .o4(byte_storage_13_o4),
    .o5(byte_storage_13_o5), .o6(byte_storage_13_o6), .o7(byte_storage_13_o7), .o8(byte_storage_13_o8));
  and and_13 (and_13_out, not_1_out, decoder_1_out12);
  byte_storage byte_storage_14 (
    .o2(byte_storage_14_o2), .o3(byte_storage_14_o3), .o1(byte_storage_14_o1), .b8(b8), .b7(b7), .b6(b6),
    .b5(b5), .b4(b4), .b3(b3), .b2(b2), .b1(b1), .Enable(and_14_out), .Clock(CLK), .o4(byte_storage_14_o4),
    .o5(byte_storage_14_o5), .o6(byte_storage_14_o6), .o7(byte_storage_14_o7), .o8(byte_storage_14_o8));
  and and_14 (and_14_out, not_1_out, decoder_1_out13);
  byte_storage byte_storage_15 (
    .o2(byte_storage_15_o2), .o3(byte_storage_15_o3), .o1(byte_storage_15_o1), .b8(b8), .b7(b7), .b6(b6),
    .b5(b5), .b4(b4), .b3(b3), .b2(b2), .b1(b1), .Enable(and_15_out), .Clock(CLK), .o4(byte_storage_15_o4),
    .o5(byte_storage_15_o5), .o6(byte_storage_15_o6), .o7(byte_storage_15_o7), .o8(byte_storage_15_o8));
  and and_15 (and_15_out, not_1_out, decoder_1_out14);
  byte_storage byte_storage_16 (
    .o2(byte_storage_16_o2), .o3(byte_storage_16_o3), .o1(byte_storage_16_o1), .b8(b8), .b7(b7), .b6(b6),
    .b5(b5), .b4(b4), .b3(b3), .b2(b2), .b1(b1), .Enable(and_16_out), .Clock(CLK), .o4(byte_storage_16_o4),
    .o5(byte_storage_16_o5), .o6(byte_storage_16_o6), .o7(byte_storage_16_o7), .o8(byte_storage_16_o8));
  and and_16 (and_16_out, not_1_out, decoder_1_out15);
  Decoder #(.select(4), .enable("false")) decoder_1 (
    .out0(decoder_1_out0), .out1(decoder_1_out1), .out2(decoder_1_out2), .out3(decoder_1_out3),
    .out4(decoder_1_out4), .out5(decoder_1_out5), .out6(decoder_1_out6), .out7(decoder_1_out7),
    .out8(decoder_1_out8), .out9(decoder_1_out9), .out10(decoder_1_out10), .out11(decoder_1_out11),
    .out12(decoder_1_out12), .out13(decoder_1_out13), .out14(decoder_1_out14), .out15(decoder_1_out15),
    .sel({addr4, addr3, addr2, addr1}));
  read_passing read_passing_1 (
    .o1(o1), .b8(read_passing_2_o8), .b7(read_passing_2_o7), .b6(read_passing_2_o6), .b5(read_passing_2_o5),
    .b4(read_passing_2_o4), .b3(read_passing_2_o3), .b2(read_passing_2_o2), .b1(read_passing_2_o1),
    .n8(byte_storage_1_o8), .n7(byte_storage_1_o7), .n6(byte_storage_1_o6), .n5(byte_storage_1_o5),
    .n4(byte_storage_1_o4), .n3(byte_storage_1_o3), .n2(byte_storage_1_o2), .n1(byte_storage_1_o1),
    .Enable(decoder_1_out0), .o2(o2), .o3(o3), .o4(o4), .o5(o5), .o6(o6), .o7(o7), .o8(o8));
  read_passing read_passing_2 (
    .o1(read_passing_2_o1), .b8(read_passing_3_o8), .b7(read_passing_3_o7), .b6(read_passing_3_o6),
    .b5(read_passing_3_o5), .b4(read_passing_3_o4), .b3(read_passing_3_o3), .b2(read_passing_3_o2),
    .b1(read_passing_3_o1), .n8(byte_storage_2_o8), .n7(byte_storage_2_o7), .n6(byte_storage_2_o6),
    .n5(byte_storage_2_o5), .n4(byte_storage_2_o4), .n3(byte_storage_2_o3), .n2(byte_storage_2_o2),
    .n1(byte_storage_2_o1), .Enable(decoder_1_out1), .o2(read_passing_2_o2), .o3(read_passing_2_o3),
    .o4(read_passing_2_o4), .o5(read_passing_2_o5), .o6(read_passing_2_o6), .o7(read_passing_2_o7),
    .o8(read_passing_2_o8));
  read_passing read_passing_3 (
    .o1(read_passing_3_o1), .b8(read_passing_4_o8), .b7(read_passing_4_o7), .b6(read_passing_4_o6),
    .b5(read_passing_4_o5), .b4(read_passing_4_o4), .b3(read_passing_4_o3), .b2(read_passing_4_o2),
    .b1(read_passing_4_o1), .n8(byte_storage_3_o8), .n7(byte_storage_3_o7), .n6(byte_storage_3_o6),
    .n5(byte_storage_3_o5), .n4(byte_storage_3_o4), .n3(byte_storage_3_o3), .n2(byte_storage_3_o2),
    .n1(byte_storage_3_o1), .Enable(decoder_1_out2), .o2(read_passing_3_o2), .o3(read_passing_3_o3),
    .o4(read_passing_3_o4), .o5(read_passing_3_o5), .o6(read_passing_3_o6), .o7(read_passing_3_o7),
    .o8(read_passing_3_o8));
  read_passing read_passing_4 (
    .o1(read_passing_4_o1), .b8(read_passing_5_o8), .b7(read_passing_5_o7), .b6(read_passing_5_o6),
    .b5(read_passing_5_o5), .b4(read_passing_5_o4), .b3(read_passing_5_o3), .b2(read_passing_5_o2),
    .b1(read_passing_5_o1), .n8(byte_storage_4_o8), .n7(byte_storage_4_o7), .n6(byte_storage_4_o6),
    .n5(byte_storage_4_o5), .n4(byte_storage_4_o4), .n3(byte_storage_4_o3), .n2(byte_storage_4_o2),
    .n1(byte_storage_4_o1), .Enable(decoder_1_out3), .o2(read_passing_4_o2), .o3(read_passing_4_o3),
    .o4(read_passing_4_o4), .o5(read_passing_4_o5), .o6(read_passing_4_o6), .o7(read_passing_4_o7),
    .o8(read_passing_4_o8));
  read_passing read_passing_5 (
    .o1(read_passing_5_o1), .b8(read_passing_6_o8), .b7(read_passing_6_o7), .b6(read_passing_6_o6),
    .b5(read_passing_6_o5), .b4(read_passing_6_o4), .b3(read_passing_6_o3), .b2(read_passing_6_o2),
    .b1(read_passing_6_o1), .n8(byte_storage_5_o8), .n7(byte_storage_5_o7), .n6(byte_storage_5_o6),
    .n5(byte_storage_5_o5), .n4(byte_storage_5_o4), .n3(byte_storage_5_o3), .n2(byte_storage_5_o2),
    .n1(byte_storage_5_o1), .Enable(decoder_1_out4), .o2(read_passing_5_o2), .o3(read_passing_5_o3),
    .o4(read_passing_5_o4), .o5(read_passing_5_o5), .o6(read_passing_5_o6), .o7(read_passing_5_o7),
    .o8(read_passing_5_o8));
  read_passing read_passing_6 (
    .o1(read_passing_6_o1), .b8(read_passing_7_o8), .b7(read_passing_7_o7), .b6(read_passing_7_o6),
    .b5(read_passing_7_o5), .b4(read_passing_7_o4), .b3(read_passing_7_o3), .b2(read_passing_7_o2),
    .b1(read_passing_7_o1), .n8(byte_storage_6_o8), .n7(byte_storage_6_o7), .n6(byte_storage_6_o6),
    .n5(byte_storage_6_o5), .n4(byte_storage_6_o4), .n3(byte_storage_6_o3), .n2(byte_storage_6_o2),
    .n1(byte_storage_6_o1), .Enable(decoder_1_out5), .o2(read_passing_6_o2), .o3(read_passing_6_o3),
    .o4(read_passing_6_o4), .o5(read_passing_6_o5), .o6(read_passing_6_o6), .o7(read_passing_6_o7),
    .o8(read_passing_6_o8));
  read_passing read_passing_7 (
    .o1(read_passing_7_o1), .b8(read_passing_8_o8), .b7(read_passing_8_o7), .b6(read_passing_8_o6),
    .b5(read_passing_8_o5), .b4(read_passing_8_o4), .b3(read_passing_8_o3), .b2(read_passing_8_o2),
    .b1(read_passing_8_o1), .n8(byte_storage_7_o8), .n7(byte_storage_7_o7), .n6(byte_storage_7_o6),
    .n5(byte_storage_7_o5), .n4(byte_storage_7_o4), .n3(byte_storage_7_o3), .n2(byte_storage_7_o2),
    .n1(byte_storage_7_o1), .Enable(decoder_1_out6), .o2(read_passing_7_o2), .o3(read_passing_7_o3),
    .o4(read_passing_7_o4), .o5(read_passing_7_o5), .o6(read_passing_7_o6), .o7(read_passing_7_o7),
    .o8(read_passing_7_o8));
  read_passing read_passing_8 (
    .o1(read_passing_8_o1), .b8(read_passing_9_o8), .b7(read_passing_9_o7), .b6(read_passing_9_o6),
    .b5(read_passing_9_o5), .b4(read_passing_9_o4), .b3(read_passing_9_o3), .b2(read_passing_9_o2),
    .b1(read_passing_9_o1), .n8(byte_storage_8_o8), .n7(byte_storage_8_o7), .n6(byte_storage_8_o6),
    .n5(byte_storage_8_o5), .n4(byte_storage_8_o4), .n3(byte_storage_8_o3), .n2(byte_storage_8_o2),
    .n1(byte_storage_8_o1), .Enable(decoder_1_out7), .o2(read_passing_8_o2), .o3(read_passing_8_o3),
    .o4(read_passing_8_o4), .o5(read_passing_8_o5), .o6(read_passing_8_o6), .o7(read_passing_8_o7),
    .o8(read_passing_8_o8));
  read_passing read_passing_9 (
    .o1(read_passing_9_o1), .b8(read_passing_10_o8), .b7(read_passing_10_o7), .b6(read_passing_10_o6),
    .b5(read_passing_10_o5), .b4(read_passing_10_o4), .b3(read_passing_10_o3), .b2(read_passing_10_o2),
    .b1(read_passing_10_o1), .n8(byte_storage_9_o8), .n7(byte_storage_9_o7), .n6(byte_storage_9_o6),
    .n5(byte_storage_9_o5), .n4(byte_storage_9_o4), .n3(byte_storage_9_o3), .n2(byte_storage_9_o2),
    .n1(byte_storage_9_o1), .Enable(decoder_1_out8), .o2(read_passing_9_o2), .o3(read_passing_9_o3),
    .o4(read_passing_9_o4), .o5(read_passing_9_o5), .o6(read_passing_9_o6), .o7(read_passing_9_o7),
    .o8(read_passing_9_o8));
  read_passing read_passing_10 (
    .o1(read_passing_10_o1), .b8(read_passing_11_o8), .b7(read_passing_11_o7), .b6(read_passing_11_o6),
    .b5(read_passing_11_o5), .b4(read_passing_11_o4), .b3(read_passing_11_o3), .b2(read_passing_11_o2),
    .b1(read_passing_11_o1), .n8(byte_storage_10_o8), .n7(byte_storage_10_o7), .n6(byte_storage_10_o6),
    .n5(byte_storage_10_o5), .n4(byte_storage_10_o4), .n3(byte_storage_10_o3), .n2(byte_storage_10_o2),
    .n1(byte_storage_10_o1), .Enable(decoder_1_out9), .o2(read_passing_10_o2), .o3(read_passing_10_o3),
    .o4(read_passing_10_o4), .o5(read_passing_10_o5), .o6(read_passing_10_o6), .o7(read_passing_10_o7),
    .o8(read_passing_10_o8));
  read_passing read_passing_11 (
    .o1(read_passing_11_o1), .b8(read_passing_12_o8), .b7(read_passing_12_o7), .b6(read_passing_12_o6),
    .b5(read_passing_12_o5), .b4(read_passing_12_o4), .b3(read_passing_12_o3), .b2(read_passing_12_o2),
    .b1(read_passing_12_o1), .n8(byte_storage_11_o8), .n7(byte_storage_11_o7), .n6(byte_storage_11_o6),
    .n5(byte_storage_11_o5), .n4(byte_storage_11_o4), .n3(byte_storage_11_o3), .n2(byte_storage_11_o2),
    .n1(byte_storage_11_o1), .Enable(decoder_1_out10), .o2(read_passing_11_o2), .o3(read_passing_11_o3),
    .o4(read_passing_11_o4), .o5(read_passing_11_o5), .o6(read_passing_11_o6), .o7(read_passing_11_o7),
    .o8(read_passing_11_o8));
  read_passing read_passing_12 (
    .o1(read_passing_12_o1), .b8(read_passing_13_o8), .b7(read_passing_13_o7), .b6(read_passing_13_o6),
    .b5(read_passing_13_o5), .b4(read_passing_13_o4), .b3(read_passing_13_o3), .b2(read_passing_13_o2),
    .b1(read_passing_13_o1), .n8(byte_storage_12_o8), .n7(byte_storage_12_o7), .n6(byte_storage_12_o6),
    .n5(byte_storage_12_o5), .n4(byte_storage_12_o4), .n3(byte_storage_12_o3), .n2(byte_storage_12_o2),
    .n1(byte_storage_12_o1), .Enable(decoder_1_out11), .o2(read_passing_12_o2), .o3(read_passing_12_o3),
    .o4(read_passing_12_o4), .o5(read_passing_12_o5), .o6(read_passing_12_o6), .o7(read_passing_12_o7),
    .o8(read_passing_12_o8));
  read_passing read_passing_13 (
    .o1(read_passing_13_o1), .b8(read_passing_14_o8), .b7(read_passing_14_o7), .b6(read_passing_14_o6),
    .b5(read_passing_14_o5), .b4(read_passing_14_o4), .b3(read_passing_14_o3), .b2(read_passing_14_o2),
    .b1(read_passing_14_o1), .n8(byte_storage_13_o8), .n7(byte_storage_13_o7), .n6(byte_storage_13_o6),
    .n5(byte_storage_13_o5), .n4(byte_storage_13_o4), .n3(byte_storage_13_o3), .n2(byte_storage_13_o2),
    .n1(byte_storage_13_o1), .Enable(decoder_1_out12), .o2(read_passing_13_o2), .o3(read_passing_13_o3),
    .o4(read_passing_13_o4), .o5(read_passing_13_o5), .o6(read_passing_13_o6), .o7(read_passing_13_o7),
    .o8(read_passing_13_o8));
  read_passing read_passing_14 (
    .o1(read_passing_14_o1), .b8(read_passing_15_o8), .b7(read_passing_15_o7), .b6(read_passing_15_o6),
    .b5(read_passing_15_o5), .b4(read_passing_15_o4), .b3(read_passing_15_o3), .b2(read_passing_15_o2),
    .b1(read_passing_15_o1), .n8(byte_storage_14_o8), .n7(byte_storage_14_o7), .n6(byte_storage_14_o6),
    .n5(byte_storage_14_o5), .n4(byte_storage_14_o4), .n3(byte_storage_14_o3), .n2(byte_storage_14_o2),
    .n1(byte_storage_14_o1), .Enable(decoder_1_out13), .o2(read_passing_14_o2), .o3(read_passing_14_o3),
    .o4(read_passing_14_o4), .o5(read_passing_14_o5), .o6(read_passing_14_o6), .o7(read_passing_14_o7),
    .o8(read_passing_14_o8));
  read_passing read_passing_15 (
    .o1(read_passing_15_o1), .b8(read_passing_16_o8), .b7(read_passing_16_o7), .b6(read_passing_16_o6),
    .b5(read_passing_16_o5), .b4(read_passing_16_o4), .b3(read_passing_16_o3), .b2(read_passing_16_o2),
    .b1(read_passing_16_o1), .n8(byte_storage_15_o8), .n7(byte_storage_15_o7), .n6(byte_storage_15_o6),
    .n5(byte_storage_15_o5), .n4(byte_storage_15_o4), .n3(byte_storage_15_o3), .n2(byte_storage_15_o2),
    .n1(byte_storage_15_o1), .Enable(decoder_1_out14), .o2(read_passing_15_o2), .o3(read_passing_15_o3),
    .o4(read_passing_15_o4), .o5(read_passing_15_o5), .o6(read_passing_15_o6), .o7(read_passing_15_o7),
    .o8(read_passing_15_o8));
  read_passing read_passing_16 (
    .o1(read_passing_16_o1), .n8(byte_storage_16_o8), .n7(byte_storage_16_o7), .n6(byte_storage_16_o6),
    .n5(byte_storage_16_o5), .n4(byte_storage_16_o4), .n3(byte_storage_16_o3), .n2(byte_storage_16_o2),
    .n1(byte_storage_16_o1), .Enable(decoder_1_out15), .o2(read_passing_16_o2), .o3(read_passing_16_o3),
    .o4(read_passing_16_o4), .o5(read_passing_16_o5), .o6(read_passing_16_o6), .o7(read_passing_16_o7),
    .o8(read_passing_16_o8));  // open: b8, b7, b6, b5, b4, b3, b2, b1
endmodule

module byte_storage (
  input  Clock,
  input  Enable,
  input  b1,
  input  b2,
  input  b3,
  input  b4,
  input  b5,
  input  b6,
  input  b7,
  input  b8,
  output o1,
  output o2,
  output o3,
  output o4,
  output o5,
  output o6,
  output o7,
  output o8
);

  wire and_1_out, and_2_out, and_3_out, and_4_out, and_5_out, and_6_out, and_7_out, and_8_out, and_9_out,
       and_10_out, and_11_out, and_12_out, and_13_out, and_14_out, and_15_out, and_16_out;

  J_K_Flip_Flop j_k_ff_1 (.J(and_1_out), .K(and_2_out), .clk(Clock), .Q(o1));  // open: Qn, preset, reset
  and and_1 (and_1_out, Enable, b1);
  and and_2 (and_2_out, Enable, ~b1);  // AND_Gate
  J_K_Flip_Flop j_k_ff_2 (.J(and_3_out), .K(and_4_out), .clk(Clock), .Q(o2));  // open: Qn, preset, reset
  and and_3 (and_3_out, Enable, b2);
  and and_4 (and_4_out, Enable, ~b2);  // AND_Gate
  and and_5 (and_5_out, Enable, b3);
  J_K_Flip_Flop j_k_ff_3 (.J(and_5_out), .K(and_6_out), .clk(Clock), .Q(o3));  // open: Qn, preset, reset
  and and_6 (and_6_out, Enable, ~b3);  // AND_Gate
  and and_7 (and_7_out, Enable, b4);
  J_K_Flip_Flop j_k_ff_4 (.J(and_7_out), .K(and_8_out), .clk(Clock), .Q(o4));  // open: Qn, preset, reset
  and and_8 (and_8_out, Enable, ~b4);  // AND_Gate
  J_K_Flip_Flop j_k_ff_5 (.J(and_9_out), .K(and_10_out), .clk(Clock), .Q(o5));  // open: Qn, preset, reset
  and and_9 (and_9_out, Enable, b5);
  and and_10 (and_10_out, Enable, ~b5);  // AND_Gate
  J_K_Flip_Flop j_k_ff_6 (.J(and_11_out), .K(and_12_out), .clk(Clock), .Q(o6));  // open: Qn, preset, reset
  and and_11 (and_11_out, Enable, b6);
  and and_12 (and_12_out, Enable, ~b6);  // AND_Gate
  and and_13 (and_13_out, Enable, b7);
  J_K_Flip_Flop j_k_ff_7 (.J(and_13_out), .K(and_14_out), .clk(Clock), .Q(o7));  // open: Qn, preset, reset
  and and_14 (and_14_out, Enable, ~b7);  // AND_Gate
  J_K_Flip_Flop j_k_ff_8 (.J(and_15_out), .K(and_16_out), .clk(Clock), .Q(o8));  // open: Qn, preset, reset
  and and_15 (and_15_out, Enable, b8);
  and and_16 (and_16_out, Enable, ~b8);  // AND_Gate
endmodule

module read_passing (
  input  Enable,
  input  n1,
  input  n2,
  input  n3,
  input  n4,
  input  n5,
  input  n6,
  input  n7,
  input  n8,
  input  b1,
  input  b2,
  input  b3,
  input  b4,
  input  b5,
  input  b6,
  input  b7,
  input  b8,
  output o1,
  output o2,
  output o3,
  output o4,
  output o5,
  output o6,
  output o7,
  output o8
);

  wire and_1_out, and_2_out, and_3_out, and_4_out, and_5_out, and_6_out, and_7_out, and_8_out;

  and and_1 (and_1_out, n1, Enable);
  or or_1 (o1, and_1_out, b1);
  and and_2 (and_2_out, n2, Enable);
  or or_2 (o2, and_2_out, b2);
  and and_3 (and_3_out, n3, Enable);
  and and_4 (and_4_out, n4, Enable);
  and and_5 (and_5_out, n5, Enable);
  and and_6 (and_6_out, n6, Enable);
  and and_7 (and_7_out, n7, Enable);
  and and_8 (and_8_out, n8, Enable);
  or or_3 (o3, and_3_out, b3);
  or or_4 (o4, and_4_out, b4);
  or or_5 (o5, and_5_out, b5);
  or or_6 (o6, and_6_out, b6);
  or or_7 (o7, and_7_out, b7);
  or or_8 (o8, and_8_out, b8);
endmodule
