// Logisim project CU.circ as structural Verilog: 1 circuit, main circuit CU
module CU (
  input  [7:0] Instruction,
  input  [7:0] MBR,
  input  [3:0] Counter,
  input  RegEqual,
  input  [7:0] Aout,
  input  [2:0] ALUstatus,
  input  [7:0] RegisterIn,
  output [3:0] Address,
  output Bit4,
  output Stop,
  output ALUOp,
  output WriteRegister,
  output Prt,
  output Inp,
  output MBRWrite,
  output [7:0] Data,
  output WriteInstruction,
  output [7:0] DataToReg,
  output BranchAddr
);

  wire and_1_out, and_2_out, and_3_out, and_4_out, and_5_out, and_6_out, and_8_out, decoder_1_out1,
       decoder_1_out2, decoder_1_out3, decoder_1_out4, decoder_1_out5, decoder_1_out6, decoder_1_out7,
       decoder_1_out8, decoder_1_out9, decoder_1_out10, decoder_1_out11, decoder_1_out12, decoder_1_out13,
       decoder_2_out3, decoder_2_out5, decoder_2_out7, decoder_2_out9, decoder_2_out11, decoder_2_out13,
       decoder_2_out15, or_6_out, or_7_out, or_9_out, or_10_out;
  wire [7:0] multiplexer_2_out;
  wire [7:4] or_1_out;

  Decoder #(.select(4), .enable("false")) decoder_1 (
    .out0(Stop), .out1(decoder_1_out1), .out2(decoder_1_out2), .out3(decoder_1_out3), .out4(decoder_1_out4),
    .out5(decoder_1_out5), .out6(decoder_1_out6), .out7(decoder_1_out7), .out8(decoder_1_out8),
    .out9(decoder_1_out9), .out10(decoder_1_out10), .out11(decoder_1_out11), .out12(decoder_1_out12),
    .out13(decoder_1_out13), .sel(Instruction[7:4]));  // open: out14, out15
  Decoder #(.select(4), .enable("false")) decoder_2 (
    .out3(decoder_2_out3), .out4(WriteInstruction), .out5(decoder_2_out5), .out7(decoder_2_out7),
    .out9(decoder_2_out9), .out11(decoder_2_out11), .out13(decoder_2_out13), .out15(decoder_2_out15),
    .sel(Counter));  // open: out0, out1, out2, out6, out8, out10, out12, out14
  or or_1 (or_1_out[4], ALUstatus[0], ALUstatus[1]);
  Multiplexer #(.enable("false")) multiplexer_1 (.in0(Instruction[4]), .in1(1'b0), .out(Bit4), .sel(and_1_out));
  and and_1 (and_1_out, or_10_out, decoder_2_out13);
  or or_2 (Inp, decoder_1_out13, decoder_1_out12);
  and and_2 (and_2_out, ~Inp, decoder_2_out9);  // AND_Gate
  or or_3 (MBRWrite, decoder_2_out3, decoder_2_out5, and_2_out);
  and and_3 (and_3_out, decoder_2_out15, RegEqual);
  or or_4 (or_1_out[7], decoder_1_out9, decoder_1_out8);
  or or_5 (Prt, decoder_1_out11, decoder_1_out10);
  and and_4 (and_4_out, decoder_1_out4, and_3_out);
  and and_5 (and_5_out, ~and_3_out, decoder_1_out5);  // AND_Gate
  or or_6 (or_6_out, decoder_1_out7, decoder_1_out6);
  or or_7 (or_7_out, Inp, or_6_out);
  Multiplexer #(.width(8), .enable("false")) multiplexer_2 (
    .in0(MBR), .in1({or_1_out[7], Prt, Stop, or_1_out[4], Instruction[3:0]}), .out(multiplexer_2_out),
    .sel(decoder_2_out7));
  or or_8 (BranchAddr, and_4_out, and_5_out);
  and and_6 (and_6_out, or_7_out, decoder_2_out13);
  Multiplexer #(.width(8), .enable("false")) multiplexer_3 (
    .in0(multiplexer_2_out), .in1(RegisterIn), .out(Data), .sel(or_9_out));
  or or_9 (or_9_out, decoder_2_out13, decoder_2_out11);
  // Probe on {or_1_out[7], Prt, Stop, or_1_out[4], Instruction[3:0]}
  or or_10 (or_10_out, decoder_1_out2, decoder_1_out3);
  and and_7 (ALUOp, or_10_out, decoder_2_out11);
  and and_8 (and_8_out, or_10_out, decoder_2_out13);
  or or_11 (WriteRegister, and_8_out, and_6_out);
  Multiplexer #(.width(8), .enable("false")) multiplexer_4 (.in0(Aout), .in1(MBR), .out(DataToReg), .sel(and_6_out));

  assign Address = Instruction[3:0];

  // Notes on the sheet:
  //   9. Write to MBR if OP is not input
  //   Zero_Neg_Over
  //   Contains registers or 0 for add/sub
  //   Ld
  //   Str
  //   Add
  //   Beq
  //   Bnq
  //   Sub
  //   Send register data
  //   Special Data for Step 4
  //   There is a delay for instruction, therefore it is tick 2 + 1
endmodule
