// Logisim project Four_Bits_Add_Sub.circ as structural Verilog: 4 circuits, main circuit Add_Sub_4Bits
module Add_Sub_4Bits (
  input  [3:0] A,
  input  [3:0] B,
  input  Add_Sub,
  output [3:0] R,
  output Zero,
  output Overflow
);

  wire add_1bit_1_cout, add_1bit_2_cout, add_1bit_3_cout, not_1_out, twos_comp_1_aout, twos_comp_1_bout,
       twos_comp_1_cout, twos_comp_1_dout;

  // Probe on A
  // Probe on B
  not not_1 (not_1_out, Add_Sub);
  Twos_Comp twos_comp_1 (
    .Enable(not_1_out), .A(B[0]), .B(B[1]), .C(B[2]), .D(B[3]), .Aout(twos_comp_1_aout),
    .Bout(twos_comp_1_bout), .Cout(twos_comp_1_cout), .Dout(twos_comp_1_dout));  // open: Overflow
  Add_1Bit add_1bit_1 (.A(twos_comp_1_aout), .Cout(add_1bit_1_cout), .B(A[0]), .Sum(R[0]));  // open: Cin
  Add_1Bit add_1bit_2 (.A(twos_comp_1_bout), .Cout(add_1bit_2_cout), .B(A[1]), .Sum(R[1]), .Cin(add_1bit_1_cout));
  Add_1Bit add_1bit_3 (.A(twos_comp_1_cout), .Cout(add_1bit_3_cout), .B(A[2]), .Sum(R[2]), .Cin(add_1bit_2_cout));
  Add_1Bit add_1bit_4 (.A(twos_comp_1_dout), .B(A[3]), .Sum(R[3]), .Cin(add_1bit_3_cout));  // open: Cout
  // Probe on R
  and and_1 (Zero, ~R[0], ~R[1], ~R[2], ~R[3], ~Overflow);  // AND_Gate
  Overfloww overfloww_1 (.Ain(A[3]), .Bin(twos_comp_1_dout), .Rout(R[3]), .Overflow(Overflow));

  // Notes on the sheet:
  //   Allan Wang - 260667681
endmodule

module Add_1Bit (
  input  Cin,
  input  A,
  input  B,
  output Sum,
  output Cout
);

  wire and_1_out, and_2_out, and_3_out, and_4_out, and_5_out, not_1_out, or_1_out;

  and and_1 (and_1_out, Cin, A, B);
  or or_1 (or_1_out, Cin, A, B);
  not not_1 (not_1_out, Cout);
  and and_2 (and_2_out, A, B);
  and and_3 (and_3_out, A, Cin);
  and and_4 (and_4_out, B, Cin);
  and and_5 (and_5_out, or_1_out, not_1_out);
  or or_2 (Cout, and_2_out, and_3_out, and_4_out);
  or or_3 (Sum, and_1_out, and_5_out);

  // Notes on the sheet:
  //   YOUR NAME AND STUDENT NUMBER HERE
endmodule

module Twos_Comp (
  input  Enable,
  input  A,
  input  B,
  input  C,
  input  D,
  output Aout,
  output Bout,
  output Cout,
  output Dout,
  output Overflow
);

  wire add_1bit_1_cout, add_1bit_1_sum, add_1bit_2_cout, add_1bit_2_sum, add_1bit_3_cout, add_1bit_3_sum,
       add_1bit_4_cout, add_1bit_4_sum, and_1_out, and_2_out, and_3_out, and_4_out, and_5_out, and_6_out,
       and_7_out, and_8_out, not_1_out, not_2_out, not_3_out, not_4_out;

  not not_1 (not_1_out, A);
  not not_2 (not_2_out, B);
  not not_3 (not_3_out, C);
  not not_4 (not_4_out, D);
  and and_1 (and_1_out, Enable, add_1bit_1_sum);
  Add_1Bit add_1bit_1 (.A(not_1_out), .Cout(add_1bit_1_cout), .Sum(add_1bit_1_sum), .Cin(Enable));  // open: B
  and and_2 (and_2_out, ~Enable, A);  // AND_Gate
  and and_3 (and_3_out, Enable, add_1bit_2_sum);
  Add_1Bit add_1bit_2 (.A(not_2_out), .Cout(add_1bit_2_cout), .Sum(add_1bit_2_sum), .Cin(add_1bit_1_cout));  // open: B
  and and_4 (and_4_out, ~Enable, B);  // AND_Gate
  and and_5 (and_5_out, Enable, add_1bit_3_sum);
  Add_1Bit add_1bit_3 (.A(not_3_out), .Cout(add_1bit_3_cout), .Sum(add_1bit_3_sum), .Cin(add_1bit_2_cout));  // open: B
  and and_6 (and_6_out, ~Enable, C);  // AND_Gate
  and and_7 (and_7_out, Enable, add_1bit_4_sum);
  Add_1Bit add_1bit_4 (.A(not_4_out), .Cout(add_1bit_4_cout), .Sum(add_1bit_4_sum), .Cin(add_1bit_3_cout));  // open: B
  and and_8 (and_8_out, ~Enable, D);  // AND_Gate
  and and_9 (Overflow, Enable, add_1bit_4_cout);
  or or_1 (Aout, and_1_out, and_2_out);
  or or_2 (Bout, and_3_out, and_4_out);
  or or_3 (Cout, and_5_out, and_6_out);
  or or_4 (Dout, and_7_out, and_8_out);
endmodule

module Overfloww (
  input  Ain,
  input  Bin,
  input  Rout,
  output Overflow
);

  wire and_1_out, and_2_out;

  and and_1 (and_1_out, Ain, Bin, ~Rout);  // AND_Gate
  and and_2 (and_2_out, ~Ain, ~Bin, Rout);  // AND_Gate
  or or_1 (Overflow, and_1_out, and_2_out);

  // Notes on the sheet:
  //   Overflows occure when + and + -> - or - and - -> +
endmodule
