// Logisim project Memory16.circ as structural Verilog: 3 circuits, main circuit byte_storage_compact
module byte_storage_compact (
  input  Clock,
  input  EnableWrite,
  input  [7:0] in_3,
  output [7:0] out_4
);

  wire and_1_out, and_2_out, and_3_out, and_4_out, and_5_out, and_6_out, and_7_out, and_8_out, and_9_out,
       and_10_out, and_11_out, and_12_out, and_13_out, and_14_out, and_15_out, and_16_out;

  J_K_Flip_Flop j_k_ff_1 (.J(and_1_out), .K(and_2_out), .clk(Clock), .Q(out_4[0]));  // open: Qn, preset, reset
  and and_1 (and_1_out, EnableWrite, in_3[0]);
  and and_2 (and_2_out, EnableWrite, ~in_3[0]);  // AND_Gate
  J_K_Flip_Flop j_k_ff_2 (.J(and_3_out), .K(and_4_out), .clk(Clock), .Q(out_4[1]));  // open: Qn, preset, reset
  and and_3 (and_3_out, EnableWrite, in_3[1]);
  and and_4 (and_4_out, EnableWrite, ~in_3[1]);  // AND_Gate
  and and_5 (and_5_out, EnableWrite, in_3[2]);
  J_K_Flip_Flop j_k_ff_3 (.J(and_5_out), .K(and_6_out), .clk(Clock), .Q(out_4[2]));  // open: Qn, preset, reset
  and and_6 (and_6_out, EnableWrite, ~in_3[2]);  // AND_Gate
  J_K_Flip_Flop j_k_ff_4 (.J(and_7_out), .K(and_8_out), .clk(Clock), .Q(out_4[3]));  // open: Qn, preset, reset
  and and_7 (and_7_out, EnableWrite, in_3[3]);
  and and_8 (and_8_out, EnableWrite, ~in_3[3]);  // AND_Gate
  J_K_Flip_Flop j_k_ff_5 (.J(and_9_out), .K(and_10_out), .clk(Clock), .Q(out_4[4]));  // open: Qn, preset, reset
  and and_9 (and_9_out, EnableWrite, in_3[4]);
  and and_10 (and_10_out, EnableWrite, ~in_3[4]);  // AND_Gate
  J_K_Flip_Flop j_k_ff_6 (.J(and_11_out), .K(and_12_out), .clk(Clock), .Q(out_4[5]));  // open: Qn, preset, reset
  and and_11 (and_11_out, EnableWrite, in_3[5]);
  and and_12 (and_12_out, EnableWrite, ~in_3[5]);  // AND_Gate
  and and_13 (and_13_out, EnableWrite, in_3[6]);
  J_K_Flip_Flop j_k_ff_7 (.J(and_13_out), .K(and_14_out), .clk(Clock), .Q(out_4[6]));  // open: Qn, preset, reset
  and and_14 (and_14_out, EnableWrite, ~in_3[6]);  // AND_Gate
  J_K_Flip_Flop j_k_ff_8 (.J(and_15_out), .K(and_16_out), .clk(Clock), .Q(out_4[7]));  // open: Qn, preset, reset
  and and_15 (and_15_out, EnableWrite, in_3[7]);
  and and_16 (and_16_out, EnableWrite, ~in_3[7]);  // AND_Gate
endmodule

module RAM16C (
  input  [3:0] Addr,
  input  EnableWrite,
  input  CLK,
  input  [7:0] DataInput,
  input  ROMoverwrite,
  input  Reset,
  input  [7:0] in_7,
  input  [7:0] in_8,
  input  [7:0] in_9,
  input  [7:0] in_10,
  input  [7:0] in_11,
  input  [7:0] in_12,
  input  [7:0] in_13,
  input  [7:0] in_14,
  input  [7:0] in_15,
  input  [7:0] in_16,
  input  [7:0] in_17,
  input  [7:0] in_18,
  input  [7:0] in_19,
  input  [7:0] in_20,
  input  [7:0] in_21,
  input  [7:0] in_22,
  output [7:0] out_23
);

  wire and_1_out, and_2_out, and_3_out, and_4_out, and_5_out, and_6_out, and_7_out, and_8_out, and_9_out,
       and_10_out, and_11_out, and_12_out, and_13_out, and_14_out, and_15_out, and_16_out, decoder_1_out0,
       decoder_1_out1, decoder_1_out2, decoder_1_out3, decoder_1_out4, decoder_1_out5, decoder_1_out6,
       decoder_1_out7, decoder_1_out8, decoder_1_out9, decoder_1_out10, decoder_1_out11, decoder_1_out12,
       decoder_1_out13, decoder_1_out14, decoder_1_out15, or_1_out, or_2_out, or_3_out, or_4_out, or_5_out,
       or_6_out, or_7_out, or_8_out, or_9_out, or_10_out, or_11_out, or_12_out, or_13_out, or_14_out,
       or_15_out, or_16_out;
  wire [7:0] byte_storage_compact_1_out_4, byte_storage_compact_2_out_4, byte_storage_compact_3_out_4,
       byte_storage_compact_4_out_4, byte_storage_compact_5_out_4, byte_storage_compact_6_out_4,
       byte_storage_compact_7_out_4, byte_storage_compact_8_out_4, byte_storage_compact_9_out_4,
       byte_storage_compact_10_out_4, byte_storage_compact_11_out_4, byte_storage_compact_12_out_4,
       byte_storage_compact_13_out_4, byte_storage_compact_14_out_4, byte_storage_compact_15_out_4,
       byte_storage_compact_16_out_4, multiplexer_1_out, multiplexer_2_out, multiplexer_3_out,
       multiplexer_4_out, multiplexer_5_out, multiplexer_6_out, multiplexer_7_out, multiplexer_8_out,
       multiplexer_9_out, multiplexer_10_out, multiplexer_11_out, multiplexer_12_out, multiplexer_13_out,
       multiplexer_14_out, multiplexer_15_out, multiplexer_16_out;

  or or_1 (or_1_out, ROMoverwrite, Reset, and_1_out);
  or or_2 (or_2_out, ROMoverwrite, Reset, and_2_out);
  or or_3 (or_3_out, ROMoverwrite, Reset, and_3_out);
  or or_4 (or_4_out, ROMoverwrite, Reset, and_4_out);
  or or_5 (or_5_out, ROMoverwrite, Reset, and_5_out);
  or or_6 (or_6_out, ROMoverwrite, Reset, and_6_out);
  or or_7 (or_7_out, ROMoverwrite, Reset, and_7_out);
  or or_8 (or_8_out, ROMoverwrite, Reset, and_8_out);
  or or_9 (or_9_out, ROMoverwrite, Reset, and_9_out);
  or or_10 (or_10_out, ROMoverwrite, Reset, and_10_out);
  or or_11 (or_11_out, ROMoverwrite, Reset, and_11_out);
  or or_12 (or_12_out, ROMoverwrite, Reset, and_12_out);
  or or_13 (or_13_out, ROMoverwrite, Reset, and_13_out);
  or or_14 (or_14_out, ROMoverwrite, Reset, and_14_out);
  or or_15 (or_15_out, ROMoverwrite, Reset, and_15_out);
  or or_16 (or_16_out, ROMoverwrite, Reset, and_16_out);
  Multiplexer #(.select(2), .width(8), .enable("false")) multiplexer_1 (
    .in0(DataInput), .in1(in_7), .in2({8{1'b0}}), .in3({8{1'b0}}), .out(multiplexer_1_out),
    .sel({Reset, ROMoverwrite}));
  and and_1 (and_1_out, EnableWrite, decoder_1_out0);
  Multiplexer #(.select(2), .width(8), .enable("false")) multiplexer_2 (
    .in0(DataInput), .in1(in_8), .in2({8{1'b0}}), .in3({8{1'b0}}), .out(multiplexer_2_out),
    .sel({Reset, ROMoverwrite}));
  and and_2 (and_2_out, EnableWrite, decoder_1_out1);
  Multiplexer #(.select(2), .width(8), .enable("false")) multiplexer_3 (
    .in0(DataInput), .in1(in_9), .in2({8{1'b0}}), .in3({8{1'b0}}), .out(multiplexer_3_out),
    .sel({Reset, ROMoverwrite}));
  and and_3 (and_3_out, EnableWrite, decoder_1_out2);
  Multiplexer #(.select(2), .width(8), .enable("false")) multiplexer_4 (
    .in0(DataInput), .in1(in_10), .in2({8{1'b0}}), .in3({8{1'b0}}), .out(multiplexer_4_out),
    .sel({Reset, ROMoverwrite}));
  and and_4 (and_4_out, EnableWrite, decoder_1_out3);
  Multiplexer #(.select(2), .width(8), .enable("false")) multiplexer_5 (
    .in0(DataInput), .in1(in_11), .in2({8{1'b0}}), .in3({8{1'b0}}), .out(multiplexer_5_out),
    .sel({Reset, ROMoverwrite}));
  and and_5 (and_5_out, EnableWrite, decoder_1_out4);
  Multiplexer #(.select(2), .width(8), .enable("false")) multiplexer_6 (
    .in0(DataInput), .in1(in_12), .in2({8{1'b0}}), .in3({8{1'b0}}), .out(multiplexer_6_out),
    .sel({Reset, ROMoverwrite}));
  and and_6 (and_6_out, EnableWrite, decoder_1_out5);
  Multiplexer #(.select(2), .width(8), .enable("false")) multiplexer_7 (
    .in0(DataInput), .in1(in_13), .in2({8{1'b0}}), .in3({8{1'b0}}), .out(multiplexer_7_out),
    .sel({Reset, ROMoverwrite}));
  and and_7 (and_7_out, EnableWrite, decoder_1_out6);
  Multiplexer #(.select(2), .width(8), .enable("false")) multiplexer_8 (
    .in0(DataInput), .in1(in_14), .in2({8{1'b0}}), .in3({8{1'b0}}), .out(multiplexer_8_out),
    .sel({Reset, ROMoverwrite}));
  and and_8 (and_8_out, EnableWrite, decoder_1_out7);
  Multiplexer #(.select(2), .width(8), .enable("false")) multiplexer_9 (
    .in0(DataInput), .in1(in_15), .in2({8{1'b0}}), .in3({8{1'b0}}), .out(multiplexer_9_out),
    .sel({Reset, ROMoverwrite}));
  and and_9 (and_9_out, EnableWrite, decoder_1_out8);
  Multiplexer #(.select(2), .width(8), .enable("false")) multiplexer_10 (
    .in0(DataInput), .in1(in_16), .in2({8{1'b0}}), .in3({8{1'b0}}), .out(multiplexer_10_out),
    .sel({Reset, ROMoverwrite}));
  and and_10 (and_10_out, EnableWrite, decoder_1_out9);
  Multiplexer #(.select(2), .width(8), .enable("false")) multiplexer_11 (
    .in0(DataInput), .in1(in_17), .in2({8{1'b0}}), .in3({8{1'b0}}), .out(multiplexer_11_out),
    .sel({Reset, ROMoverwrite}));
  and and_11 (and_11_out, EnableWrite, decoder_1_out10);
  Multiplexer #(.select(2), .width(8), .enable("false")) multiplexer_12 (
    .in0(DataInput), .in1(in_18), .in2({8{1'b0}}), .in3({8{1'b0}}), .out(multiplexer_12_out),
    .sel({Reset, ROMoverwrite}));
  and and_12 (and_12_out, EnableWrite, decoder_1_out11);
  Multiplexer #(.select(2), .width(8), .enable("false")) multiplexer_13 (
    .in0(DataInput), .in1(in_19), .in2({8{1'b0}}), .in3({8{1'b0}}), .out(multiplexer_13_out),
    .sel({Reset, ROMoverwrite}));
  and and_13 (and_13_out, EnableWrite, decoder_1_out12);
  Multiplexer #(.select(2), .width(8), .enable("false")) multiplexer_14 (
    .in0(DataInput), .in1(in_20), .in2({8{1'b0}}), .in3({8{1'b0}}), .out(multiplexer_14_out),
    .sel({Reset, ROMoverwrite}));
  and and_14 (and_14_out, EnableWrite, decoder_1_out13);
  Multiplexer #(.select(2), .width(8), .enable("false")) multiplexer_15 (
    .in0(DataInput), .in1(in_21), .in2({8{1'b0}}), .in3({8{1'b0}}), .out(multiplexer_15_out),
    .sel({Reset, ROMoverwrite}));
  and and_15 (and_15_out, EnableWrite, decoder_1_out14);
  Multiplexer #(.select(2), .width(8), .enable("false")) multiplexer_16 (
    .in0(DataInput), .in1(in_22), .in2({8{1'b0}}), .in3({8{1'b0}}), .out(multiplexer_16_out),
    .sel({Reset, ROMoverwrite}));
  and and_16 (and_16_out, EnableWrite, decoder_1_out15);
  Decoder #(.select(4), .enable("false")) decoder_1 (
    .out0(decoder_1_out0), .out1(decoder_1_out1), .out2(decoder_1_out2), .out3(decoder_1_out3),
    .out4(decoder_1_out4), .out5(decoder_1_out5), .out6(decoder_1_out6), .out7(decoder_1_out7),
    .out8(decoder_1_out8), .out9(decoder_1_out9), .out10(decoder_1_out10), .out11(decoder_1_out11),
    .out12(decoder_1_out12), .out13(decoder_1_out13), .out14(decoder_1_out14), .out15(decoder_1_out15),
    .sel(Addr));
  byte_storage_compact byte_storage_compact_1 (
    .out_4(byte_storage_compact_1_out_4), .in_3(multiplexer_1_out), .EnableWrite(or_1_out), .Clock(CLK));
  byte_storage_compact byte_storage_compact_2 (
    .out_4(byte_storage_compact_2_out_4), .in_3(multiplexer_2_out), .EnableWrite(or_2_out), .Clock(CLK));
  byte_storage_compact byte_storage_compact_3 (
    .out_4(byte_storage_compact_3_out_4), .in_3(multiplexer_3_out), .EnableWrite(or_3_out), .Clock(CLK));
  byte_storage_compact byte_storage_compact_4 (
    .out_4(byte_storage_compact_4_out_4), .in_3(multiplexer_4_out), .EnableWrite(or_4_out), .Clock(CLK));
  byte_storage_compact byte_storage_compact_5 (
    .out_4(byte_storage_compact_5_out_4), .in_3(multiplexer_5_out), .EnableWrite(or_5_out), .Clock(CLK));
  byte_storage_compact byte_storage_compact_6 (
    .out_4(byte_storage_compact_6_out_4), .in_3(multiplexer_6_out), .EnableWrite(or_6_out), .Clock(CLK));
  byte_storage_compact byte_storage_compact_7 (
    .out_4(byte_storage_compact_7_out_4), .in_3(multiplexer_7_out), .EnableWrite(or_7_out), .Clock(CLK));
  byte_storage_compact byte_storage_compact_8 (
    .out_4(byte_storage_compact_8_out_4), .in_3(multiplexer_8_out), .EnableWrite(or_8_out), .Clock(CLK));
  byte_storage_compact byte_storage_compact_9 (
    .out_4(byte_storage_compact_9_out_4), .in_3(multiplexer_9_out), .EnableWrite(or_9_out), .Clock(CLK));
  byte_storage_compact byte_storage_compact_10 (
    .out_4(byte_storage_compact_10_out_4), .in_3(multiplexer_10_out), .EnableWrite(or_10_out), .Clock(CLK));
  byte_storage_compact byte_storage_compact_11 (
    .out_4(byte_storage_compact_11_out_4), .in_3(multiplexer_11_out), .EnableWrite(or_11_out), .Clock(CLK));
  byte_storage_compact byte_storage_compact_12 (
    .out_4(byte_storage_compact_12_out_4), .in_3(multiplexer_12_out), .EnableWrite(or_12_out), .Clock(CLK));
  byte_storage_compact byte_storage_compact_13 (
    .out_4(byte_storage_compact_13_out_4), .in_3(multiplexer_13_out), .EnableWrite(or_13_out), .Clock(CLK));
  byte_storage_compact byte_storage_compact_14 (
    .out_4(byte_storage_compact_14_out_4), .in_3(multiplexer_14_out), .EnableWrite(or_14_out), .Clock(CLK));
  byte_storage_compact byte_storage_compact_15 (
    .out_4(byte_storage_compact_15_out_4), .in_3(multiplexer_15_out), .EnableWrite(or_15_out), .Clock(CLK));
  byte_storage_compact byte_storage_compact_16 (
    .out_4(byte_storage_compact_16_out_4), .in_3(multiplexer_16_out), .EnableWrite(or_16_out), .Clock(CLK));
  Multiplexer #(.select(4), .width(8), .enable("false")) multiplexer_17 (
    .in0(byte_storage_compact_1_out_4), .in1(byte_storage_compact_2_out_4),
    .in2(byte_storage_compact_3_out_4), .in3(byte_storage_compact_4_out_4),
    .in4(byte_storage_compact_5_out_4), .in5(byte_storage_compact_6_out_4),
    .in6(byte_storage_compact_7_out_4), .in7(byte_storage_compact_8_out_4),
    .in8(byte_storage_compact_9_out_4), .in9(byte_storage_compact_10_out_4),
    .in10(byte_storage_compact_11_out_4), .in11(byte_storage_compact_12_out_4),
    .in12(byte_storage_compact_13_out_4), .in13(byte_storage_compact_14_out_4),
    .in14(byte_storage_compact_15_out_4), .in15(byte_storage_compact_16_out_4), .out(out_23), .sel(Addr));
  // Probe on byte_storage_compact_1_out_4
  // Probe on byte_storage_compact_2_out_4
  // Probe on byte_storage_compact_3_out_4
  // Probe on byte_storage_compact_4_out_4
  // Probe on byte_storage_compact_5_out_4
  // Probe on byte_storage_compact_6_out_4
  // Probe on byte_storage_compact_7_out_4
  // Probe on byte_storage_compact_8_out_4
  // Probe on byte_storage_compact_9_out_4
  // Probe on byte_storage_compact_10_out_4
  // Probe on byte_storage_compact_11_out_4
  // Probe on byte_storage_compact_12_out_4
  // Probe on byte_storage_compact_13_out_4
  // Probe on byte_storage_compact_14_out_4
  // Probe on byte_storage_compact_15_out_4
  // Probe on byte_storage_compact_16_out_4
endmodule

module ROM16C (
  input  Enable,
  input  [7:0] in_2,
  input  [7:0] in_3,
  input  [7:0] in_4,
  input  [7:0] in_5,
  input  [7:0] in_6,
  input  [7:0] in_7,
  input  [7:0] in_8,
  input  [7:0] in_9,
  input  [7:0] in_10,
  input  [7:0] in_11,
  input  [7:0] in_12,
  input  [7:0] in_13,
  input  [7:0] in_14,
  input  [7:0] in_15,
  input  [7:0] in_16,
  input  [7:0] in_17,
  output out_18,
  output [7:0] out_19,
  output [7:0] out_20,
  output [7:0] out_21,
  output [7:0] out_22,
  output [7:0] out_23,
  output [7:0] out_24,
  output [7:0] out_25,
  output [7:0] out_26,
  output [7:0] out_27,
  output [7:0] out_28,
  output [7:0] out_29,
  output [7:0] out_30,
  output [7:0] out_31,
  output [7:0] out_32,
  output [7:0] out_33,
  output [7:0] out_34
);


  assign out_18 = Enable;
  assign out_19 = in_2;
  assign out_20 = in_3;
  assign out_21 = in_4;
  assign out_22 = in_5;
  assign out_23 = in_6;
  assign out_24 = in_7;
  assign out_25 = in_8;
  assign out_26 = in_9;
  assign out_27 = in_10;
  assign out_28 = in_11;
  assign out_29 = in_12;
  assign out_30 = in_13;
  assign out_31 = in_14;
  assign out_32 = in_15;
  assign out_33 = in_16;
  assign out_34 = in_17;
endmodule
